# Fritzing sketch JabaraMIDI_V2 (saved by Fritzing 0.9.2b)

parts:
  M1 = S2 mini
  パーツ1 = BME280
  パーツ2 = Adafruit I2C QT Rotary Encoder [part_number="Adafruit #4991"]
  パーツ3 = BME280
  M5StickC1 = M5StickC

nets:
  N1: M1.9, M5StickC1.EXT_G0
  N2: M1.8, M5StickC1.EXT_G26
  N3: M1.11, パーツ1.SCL, パーツ3.SCL
  N4: M1.10, パーツ1.SDA, パーツ3.SDA
  VIN: M1.3.3V, パーツ1.VIN, パーツ3.VIN
  N5: M1.VBUS, M5StickC1.EXT_5V_IN
  GND: M1.GND, パーツ1.GND, パーツ3.GND, M5StickC1.EXT_GND
  N6: パーツ2.GND, M5StickC1.GROVE_GND
  N7: パーツ2.VCC, M5StickC1.GROVE_5V_OUT
  N8: パーツ2.SDA, M5StickC1.GROVE_G32
  N9: パーツ2.SCL, M5StickC1.GROVE_G33

notes:
  M5Stack Encoder Unit
  BME/BMP280
  0x77: inside
  0x76: outside
  M5StickC Plus
  Wemos Lolin S2 Mini (USB connection to PC comes here)

custom parts:
  S2 mini: S2 mini. A mini wifi board based on ESP32-S2FN4R2.
  Adafruit I2C QT Rotary Encoder: Rotary encoders are soooo much fun! Twist em this way, then twist them that way. Unlike potentiometers, they go all the way around, and often have little detents for tactile feedback. But, if you've ever tried to add encoders to your project you know that they're a real challenge to use: timers, interrupts, debouncing... This Stemma QT breakout makes all that frustration go away - solder in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
